# Fritzing sketch tcs230-schematic-diagram (saved by Fritzing 0.9.2b)

parts:
  e-radionica1 = TCS230 Color Sensor [part_number=101209]
  Componente1 = Arduino Uno (Rev3) - ICSP
  Componente2 = ws2812b [package="smd 2812b"]

nets:
  GND: e-radionica1.Gnd, Componente1.GND, Componente2.VSS
  N1: e-radionica1.S1, Componente1.D5_PWM
  N2: e-radionica1.S0, Componente1.D4
  N3: e-radionica1.S3, Componente1.D7
  N4: e-radionica1.S2, Componente1.D6_PWM
  N5: e-radionica1.Out, Componente1.D8
  VCC: e-radionica1.Vcc, Componente1.5V, Componente2.VDD
  N6: Componente1.D9_PWM, Componente2.DIN

notes:
  NeoPixel
  WS2812b
  TCS230
  RGB light/color sensor
  +5V
  GND

custom parts:
  TCS230 Color Sensor: TCS230
